# Fritzing sketch circuitDesign (saved by Fritzing 0.9.2b)

parts:
  J1 = female pin header, 2 pins [form="♀ (female)"]  # not connected
  J2 = female pin header, 2 pins [form="♀ (female)"]
  J3 = female pin header, 2 pins [form="♀ (female)"]
  J4 = female pin header, 2 pins [form="♀ (female)"]
  J5 = female pin header, 2 pins [form="♀ (female)"]
  J6 = female pin header, 2 pins [form="♀ (female)"]
  J7 = female pin header, 2 pins [form="♀ (female)"]
  J8 = female pin header, 2 pins [form="♀ (female)"]
  J9 = female pin header, 2 pins [form="♀ (female)"]  # not connected
  J10 = female pin header, 2 pins [form="♀ (female)"]
  J11 = female pin header, 2 pins [form="♀ (female)"]  # not connected
  RHT2 = Humidity and Temperature Sensor RHT03
  RHT4 = Humidity and Temperature Sensor RHT03  # not connected
  R1 = Resistor [tolerance=±5% resistance=220 package=THT]
  R2 = Resistor [tolerance=±5% resistance=220 package=THT]
  R3 = Resistor [tolerance=±5% resistance=220 package=THT]
  R4 = Resistor [tolerance=±5% resistance=220 package=THT]  # not connected
  U2 = RELAY [package=relay-jzc]
  U3 = RELAY [package=relay-jzc]
  IC1 = H-Bridge [package=THT]
  M1 = Stepper Motor - Bipolar
  U1 = RELAY [package=relay-jzc]
  Q1 = Basic FET P-Channel [package="TO220 [THT]"]
  R5 = Photocell (LDR) [package=THT]  # not connected

nets:
  N1: J2.pin1, RHT2.Data-signal
  N2: J3.pin1, IC1.2A
  N3: J3.pin2, IC1.1A
  N4: J4.pin2, R3.Pin_0
  N5: J5.pin2, R1.Pin_1
  N6: J6.pin1, U2.NC
  N7: J6.pin2, U3.NC
  N8: J7.pin1, Q1.source
  N9: J7.pin2, R2.Pin_1
  N10: J8.pin2, U1.NC
  N11: J10.pin1, IC1.3A
  N12: J10.pin2, IC1.4A
  N13: IC1.1Y, M1.D
  N14: IC1.2Y, M1.B
  N15: IC1.3Y, M1.C
  N16: IC1.4Y, M1.A

notes:
  전류 센서를 통해 사용한 전류를 측정
  DHT11 온습도 센서 두 개를 이용해 온습도 값 측정 및 정규화
  Relay Modulel을 이용해 주변 기기 원격으로 제어
  main board.
  esp8266 12E.
  L923D.
  motor driver.
  LDR.
  조도센서(빛 저)
